// Logisim project ADE_Mini_Project.circ as structural Verilog
module Full_Adder (
  input  [3:0] A,
  input  [3:0] B,
  input  [3:0] C,
  output [3:0] out_4,
  output [3:0] out_5
);

  wire [3:0] and_1_out, and_2_out, xor_1_out;

  assign xor_1_out = A ^ B;  // XOR_Gate xor_1, 4 bits wide
  assign and_1_out = C & xor_1_out;  // AND_Gate and_1, 4 bits wide
  assign out_4 = xor_1_out ^ C;  // XOR_Gate xor_2, 4 bits wide
  assign and_2_out = A & B;  // AND_Gate and_2, 4 bits wide
  assign out_5 = and_1_out | and_2_out;  // OR_Gate or_1, 4 bits wide

  // Notes on the sheet:
  //   XOR Gate
  //   AND Gate
  //   XOR Gate
  //   AND Gate
  //   SUM
  //   OR Gate
  //   CARRY out
endmodule
