// Logisim project EXOR.circ as structural Verilog: 13 circuits, main circuit main
module main (
  input  in_1,
  input  in_2,
  output out_3
);

  wire and_1_out, and_2_out, not_1_out, not_2_out;

  not not_1 (not_1_out, in_1);
  not not_2 (not_2_out, in_2);
  and and_1 (and_1_out, in_1, not_2_out);
  and and_2 (and_2_out, not_1_out, in_2);
  or or_1 (out_3, and_1_out, and_2_out);
endmodule

module EXOR (
  input  in_1,
  input  in_2,
  output out_3,
  output out_4
);

  xor xor_1 (out_3, in_1, in_2);
  and and_1 (out_4, in_1, in_2);
endmodule

module Full_Adder (
  input  [3:0] A,
  input  [3:0] B,
  output [3:0] S,
  output C
);

  wire not_1_out, or_1_out;

  Adder #(.width(4)) adder_1 (.a(A), .b(B), .out(S), .cin(1'b0), .cout(C));
  LED Z (.in(not_1_out));
  not not_1 (not_1_out, or_1_out);
  or or_1 (or_1_out, S[0], S[1], S[2], S[3]);
endmodule

module MUX (
  input  [3:0] A,
  input  [3:0] B,
  input  [1:0] C,
  output [3:0] D
);

  wire [3:0] and_1_out, not_1_out, or_1_out, xor_1_out;

  assign and_1_out = A & B;  // AND_Gate and_1, 4 bits wide
  assign or_1_out = B | A;  // OR_Gate or_1, 4 bits wide
  assign xor_1_out = B ^ A;  // XOR_Gate xor_1, 4 bits wide
  assign not_1_out = ~A;  // NOT_Gate not_1, 4 bits wide
  Multiplexer #(.select(2), .width(4)) multiplexer_1 (
    .in0(and_1_out), .in1(or_1_out), .in2(xor_1_out), .in3(not_1_out), .out(D), .sel(C));
endmodule

module Registers (
  input  [3:0] X,
  input  [1:0] in_2,
  input  [1:0] in_3,
  input  [1:0] V,
  output [3:0] Y,
  output [3:0] W
);

  wire clock_1_out, demultiplexer_1_out0, demultiplexer_1_out1, demultiplexer_1_out2, demultiplexer_1_out3;
  wire [3:0] register_1_q, register_2_q, register_3_q;

  Clock clock_1 (.out(clock_1_out));
  Demultiplexer #(.select(2)) demultiplexer_1 (
    .out0(demultiplexer_1_out0), .out1(demultiplexer_1_out1), .out2(demultiplexer_1_out2),
    .out3(demultiplexer_1_out3), .in(1'b1), .sel(V));
  Register #(.width(4)) register_1 (
    .D(X), .en(demultiplexer_1_out0), .clk(clock_1_out), .Q(register_1_q));  // open: clr
  Register #(.width(4)) register_2 (
    .D(X), .en(demultiplexer_1_out1), .clk(clock_1_out), .Q(register_2_q));  // open: clr
  Register #(.width(4)) register_3 (
    .D(X), .en(demultiplexer_1_out2), .clk(clock_1_out), .Q(register_3_q));  // open: clr
  Register #(.width(4)) register_4 (
    .D(X), .en(demultiplexer_1_out3), .clk(clock_1_out), .Q(register_3_q));  // open: clr
  Multiplexer #(.select(2), .width(4)) multiplexer_1 (
    .in0(register_1_q), .in1(register_2_q), .in2(register_3_q), .in3(register_3_q), .out(Y), .sel(in_2));
  Multiplexer #(.select(2), .width(4)) multiplexer_2 (
    .in0(register_1_q), .in1(register_2_q), .in2(register_3_q), .in3(register_3_q), .out(W), .sel(in_3));
endmodule

module Counter_New (
);

  wire clock_1_out;
  wire [3:0] counter_1_q, counter_1_q_2;

  Clock clock_1 (.out(clock_1_out));
  Counter counter_1 (
    .clr(1'b0), .load(1'b0), .up(1'b1), .count(1'b1), .clk(clock_1_out), .Q({counter_1_q_2, counter_1_q}));  // open: D, carry
  LedBar ledbar_1 (
    .led0(counter_1_q_2[3]), .led1(counter_1_q_2[2]), .led2(counter_1_q_2[1]), .led3(counter_1_q_2[0]),
    .led4(counter_1_q[3]), .led5(counter_1_q[2]), .led6(counter_1_q[1]), .led7(counter_1_q[0]));
  Hex_Digit_Display hex_digit_display_1 (.value(counter_1_q_2));  // open: dp
  Hex_Digit_Display hex_digit_display_2 (.value(counter_1_q));  // open: dp
endmodule

module CPU (
  input  [3:0] A,
  input  [3:0] B,
  input  [2:0] C,
  output [3:0] D
);

  wire [3:0] full_adder_1_s, mux_1_d;

  Full_Adder full_adder_1 (.A(A), .B(B), .S(full_adder_1_s));  // open: C
  MUX mux_1 (.A(A), .B(B), .C(C[1:0]), .D(mux_1_d));
  Multiplexer #(.width(4)) multiplexer_1 (.in0(full_adder_1_s), .in1(mux_1_d), .out(D), .sel(C[2]));
endmodule

module CPU2 (
);

  wire CLK, Data, MoveImmd, not_1_out, not_2_out;
  wire [1:0] Ra, Rb, Rd;
  wire [2:0] OP;
  wire [3:0] controlled_buffer_1_out, cpu_1_d, register_cpu_1_w, register_cpu_1_y;
  wire [7:0] counter_1_q;
  wire [15:0] rom_1_data;
  wire [15:6] register_1_q;

  Clock clock_1 (.out(CLK));
  Counter counter_1 (.clr(1'b0), .load(1'b0), .up(1'b1), .count(1'b1), .clk(CLK), .Q(counter_1_q));  // open: D, carry
  assign controlled_buffer_1_out = MoveImmd ? {Ra, Rb} : 4'bz;  // Controlled_Buffer controlled_buffer_1
  Hex_Digit_Display hex_digit_display_1 (.value(counter_1_q[7:4]));  // open: dp
  Hex_Digit_Display hex_digit_display_2 (.value(counter_1_q[3:0]));  // open: dp
  ROM #(.dataWidth(16)) rom_1 (.addr(counter_1_q), .data(rom_1_data));
  Register_CPU register_cpu_1 (
    .X(controlled_buffer_1_out), .CLK(CLK), .Ra(Ra), .Rb(Rb), .V(Rd), .Y(register_cpu_1_y),
    .W(register_cpu_1_w));
  assign controlled_buffer_1_out = Data ? cpu_1_d : 4'bz;  // Controlled_Buffer controlled_buffer_2
  Register #(.width(16)) register_1 (
    .D(rom_1_data), .en(1'b1), .clk(CLK), .Q({register_1_q[15:12], OP, register_1_q[8:6], Ra, Rb, Rd}));  // open: clr
  CPU cpu_1 (.A(register_cpu_1_y), .B(register_cpu_1_w), .C(OP), .D(cpu_1_d));
  and and_1 (MoveImmd, register_1_q[14], register_1_q[15]);
  not not_1 (not_1_out, register_1_q[14]);
  and and_2 (Data, not_1_out, not_2_out);
  not not_2 (not_2_out, register_1_q[15]);

  // Other names for the same wires on the sheet: Value[3:0] = {Ra, Rb}

  // Notes on the sheet:
  //   contents of rom_1 (hex, n*v repeats v):
  //   c009
endmodule

module Register_CPU (
  input  [3:0] X,
  input  CLK,
  input  [1:0] Ra,
  input  [1:0] Rb,
  input  [1:0] V,
  output [3:0] Y,
  output [3:0] W
);

  wire demultiplexer_1_out0, demultiplexer_1_out1, demultiplexer_1_out2, demultiplexer_1_out3;
  wire [3:0] R0_q, R1_q, R2_q, R3_q;

  Demultiplexer #(.select(2)) demultiplexer_1 (
    .out0(demultiplexer_1_out0), .out1(demultiplexer_1_out1), .out2(demultiplexer_1_out2),
    .out3(demultiplexer_1_out3), .in(1'b1), .sel(V));
  Register #(.width(4)) R0 (.D(X), .en(demultiplexer_1_out0), .clk(CLK), .Q(R0_q));  // open: clr
  Register #(.width(4)) R1 (.D(X), .en(demultiplexer_1_out1), .clk(CLK), .Q(R1_q));  // open: clr
  Register #(.width(4)) R2 (.D(X), .en(demultiplexer_1_out2), .clk(CLK), .Q(R2_q));  // open: clr
  Register #(.width(4)) R3 (.D(X), .en(demultiplexer_1_out3), .clk(CLK), .Q(R3_q));  // open: clr
  Multiplexer #(.select(2), .width(4)) multiplexer_1 (
    .in0(R0_q), .in1(R1_q), .in2(R2_q), .in3(R3_q), .out(Y), .sel(Ra));
  Multiplexer #(.select(2), .width(4)) multiplexer_2 (
    .in0(R0_q), .in1(R1_q), .in2(R2_q), .in3(R3_q), .out(W), .sel(Rb));
endmodule

module Control_Decoding_Circuit (
);

  wire CLK;
  wire [7:0] counter_1_q;
  wire [15:0] rom_1_data;

  Clock clock_1 (.out(CLK));
  Counter counter_1 (.clr(1'b0), .load(1'b0), .up(1'b1), .count(1'b1), .clk(CLK), .Q(counter_1_q));  // open: D, carry
  Hex_Digit_Display hex_digit_display_1 (.value(counter_1_q[7:4]));  // open: dp
  Hex_Digit_Display hex_digit_display_2 (.value(counter_1_q[3:0]));  // open: dp
  ROM #(.dataWidth(16)) rom_1 (.addr(counter_1_q), .data(rom_1_data));
  Register #(.width(16)) register_1 (.D(rom_1_data), .en(1'b1), .clk(CLK));  // open: Q, clr
endmodule

module Subtract (
  input  [3:0] A,
  input  [3:0] B,
  output [3:0] S,
  output C
);

  wire not_1_out, or_1_out;

  Subtractor #(.width(4)) subtractor_1 (.a(A), .b(B), .out(S), .bin(1'b0), .bout(C));
  LED Z (.in(not_1_out));
  not not_1 (not_1_out, or_1_out);
  or or_1 (or_1_out, S[0], S[1], S[2], S[3]);
endmodule

module CPU_Sub (
  input  [3:0] A,
  input  [3:0] B,
  input  [3:0] C,
  output [3:0] D
);

  wire [3:0] full_adder_1_s, mux_1_d, subtract_1_s;

  Full_Adder full_adder_1 (.A(A), .B(B), .S(full_adder_1_s));  // open: C
  Subtract subtract_1 (.A(A), .B(B), .S(subtract_1_s));  // open: C
  MUX mux_1 (.A(A), .B(B), .C(C[1:0]), .D(mux_1_d));
  Multiplexer #(.select(2), .width(4)) multiplexer_1 (
    .in0(full_adder_1_s), .in1(subtract_1_s), .in2(mux_1_d), .out(D), .sel(C[3:2]));  // open: in3
endmodule

module CPU_Sub_Final (
);

  wire CLK, Data, MoveImmd, not_1_out, not_2_out;
  wire [1:0] Ra, Rb, Rd;
  wire [3:0] controlled_buffer_1_out, cpu_sub_1_d, OP, register_cpu_1_w, register_cpu_1_y;
  wire [7:0] counter_1_q;
  wire [15:0] rom_1_data;
  wire [15:6] register_1_q;

  Clock clock_1 (.out(CLK));
  Counter counter_1 (.clr(1'b0), .load(1'b0), .up(1'b1), .count(1'b1), .clk(CLK), .Q(counter_1_q));  // open: D, carry
  assign controlled_buffer_1_out = MoveImmd ? {Ra, Rb} : 4'bz;  // Controlled_Buffer controlled_buffer_1
  Hex_Digit_Display hex_digit_display_1 (.value(counter_1_q[7:4]));  // open: dp
  Hex_Digit_Display hex_digit_display_2 (.value(counter_1_q[3:0]));  // open: dp
  ROM #(.dataWidth(16)) rom_1 (.addr(counter_1_q), .data(rom_1_data));
  Register_CPU register_cpu_1 (
    .X(controlled_buffer_1_out), .CLK(CLK), .Ra(Ra), .Rb(Rb), .V(Rd), .Y(register_cpu_1_y),
    .W(register_cpu_1_w));
  assign controlled_buffer_1_out = Data ? cpu_sub_1_d : 4'bz;  // Controlled_Buffer controlled_buffer_2
  Register #(.width(16)) register_1 (
    .D(rom_1_data), .en(1'b1), .clk(CLK), .Q({register_1_q[15:12], OP, register_1_q[7:6], Ra, Rb, Rd}));  // open: clr
  CPU_Sub cpu_sub_1 (.A(register_cpu_1_y), .B(register_cpu_1_w), .C(OP), .D(cpu_sub_1_d));
  and and_1 (MoveImmd, register_1_q[14], register_1_q[15]);
  not not_1 (not_1_out, register_1_q[14]);
  and and_2 (Data, not_1_out, not_2_out);
  not not_2 (not_2_out, register_1_q[15]);

  // Other names for the same wires on the sheet: Value[3:0] = {Ra, Rb}

  // Notes on the sheet:
  //   contents of rom_1 (hex, n*v repeats v):
  //   c018 c00a 360b
endmodule
